# Fritzing sketch Arduino-Basic-Project-#4-Fritzing-File (saved by Fritzing 0.9.3b)
breadboards: 1

parts:
  Part1 = Arduino Uno (Rev3)
  LED3 = RGB LED (com. anode, rbg) [package="5 mm [THT]"]
  R1 = Resistor [tolerance=±5% resistance=220 package=THT]
  R2 = Resistor [tolerance=±5% resistance=220 package=THT]
  R3 = Resistor [tolerance=±5% resistance=220 package=THT]

nets:
  N1: Part1.D8, R3.Pin_0
  N2: Part1.D9_PWM, R2.Pin_0
  N3: Part1.D11_PWM/MOSI, R1.Pin_0
  N4: LED3.red_cathode, R1.Pin_1
  N5: LED3.blue_cathode, R2.Pin_1
  N6: LED3.green_cathode, R3.Pin_1

notes:
  Note: Here we have used common anode type RGB LED.
